// Logisim project 8-Bit Schieberegler.circ as structural Verilog: 1 circuit, main circuit main
module main (
  input  in_1,
  input  in_2,
  input  in_3,
  input  in_4,
  input  in_5,
  input  in_6,
  input  in_7,
  input  in_8,
  input  C,
  output out_10,
  output out_11,
  output out_12,
  output out_13,
  output out_14,
  output out_15,
  output out_16,
  output out_17
);

  wire and_1_out, and_3_out, and_4_out, and_5_out, and_6_out, and_7_out, and_8_out, and_9_out, and_10_out,
       and_11_out, and_12_out, and_13_out, not_1_out;

  not not_1 (not_1_out, C);
  and and_1 (and_1_out, C, in_1);
  and and_2 (out_10, not_1_out, in_2);
  and and_3 (and_3_out, in_2, C);
  or or_1 (out_11, and_1_out, and_4_out);
  and and_4 (and_4_out, not_1_out, in_3);
  or or_2 (out_12, and_3_out, and_6_out);
  and and_5 (and_5_out, in_3, C);
  and and_6 (and_6_out, not_1_out, in_4);
  and and_7 (and_7_out, in_4, C);
  or or_3 (out_13, and_5_out, and_8_out);
  and and_8 (and_8_out, not_1_out, in_5);
  or or_4 (out_14, and_7_out, and_9_out);
  and and_9 (and_9_out, not_1_out, in_6);
  and and_10 (and_10_out, in_5, C);
  and and_11 (and_11_out, in_6, C);
  or or_5 (out_15, and_10_out, and_12_out);
  and and_12 (and_12_out, not_1_out, in_7);
  or or_6 (out_16, and_11_out, and_13_out);
  and and_13 (and_13_out, not_1_out, in_8);
  and and_14 (out_17, in_7, C);

  // Notes on the sheet:
  //   8-Bit Schieberegler
endmodule
