// Logisim project MUX und DEMUX.circ as structural Verilog: 1 circuit, main circuit main
module main (
  input  d0,
  input  d1,
  input  d2,
  input  d3,
  input  in_5,
  input  in_6,
  output d0_2,
  output d1_2,
  output d2_2,
  output d3_2
);

  wire and_1_out, and_2_out, and_3_out, and_4_out, not_1_out, not_2_out, or_1_out;

  and and_1 (and_1_out, d0, not_1_out, not_2_out);
  and and_2 (and_2_out, d1, not_1_out, in_6);
  and and_3 (and_3_out, d2, not_2_out, in_5);
  and and_4 (and_4_out, d3, in_5, in_6);
  or or_1 (or_1_out, and_1_out, and_2_out, and_3_out, and_4_out);
  not not_1 (not_1_out, in_5);
  not not_2 (not_2_out, in_6);
  and and_5 (d0_2, or_1_out, not_1_out, not_2_out);
  and and_6 (d1_2, or_1_out, not_1_out, in_6);
  and and_7 (d2_2, or_1_out, in_5, not_2_out);
  and and_8 (d3_2, or_1_out, in_5, in_6);

  // Notes on the sheet:
  //   Multiplexer
  //   s2
  //   s1
  //   Demultiplexer
endmodule
